# Fritzing sketch schematic (saved by Fritzing 0.9.10b)
breadboards: 1

parts:
  Part1 = Arduino Pro Micro (Clone)
  Part2 = Arduino Pro Micro (Clone)
  S1 = Pushbutton [package="[THT]"]
  R1 = Resistor [tolerance=±5% power=0.25 resistance=10k package=THT]
  R2 = Resistor [tolerance=±5% power=0.25 resistance=10k package=THT]
  LED1 = smd LED [color="Red (633nm)" package="0603 [SMD]"]
  LED2 = smd LED [color="Red (633nm)" package="0603 [SMD]"]

nets:
  N1: Part1.TXO, Part2.RXI
  N2: Part1.RXI, Part2.TXO
  GND: Part1.GND, Part2.GND, S1.Pin_1, S1.Pin_2, R1.Pin_1, R2.Pin_0
  N3: Part1.D9, LED1.anode
  N4: Part1.RST, Part2.RST, S1.Pin_3, S1.Pin_4
  N5: Part2.D9, LED2.anode
  N6: R1.Pin_0, LED1.cathode
  N7: R2.Pin_1, LED2.cathode
