# Fritzing sketch schematic (saved by Fritzing 0.9.10b)
breadboards: 1

parts:
  Part1 = Arduino Pro Micro (Clone)
  USBTTL1 = USB TTL Serial Cable
  J1 = male pin header, 4 pins [form="♂ (male)"]

nets:
  N1: Part1.TXO, USBTTL1.RX, J1.pin3
  N2: Part1.RXI, USBTTL1.TX, J1.pin4
  GND: Part1.GND, USBTTL1.GND, J1.pin2
  VCC: Part1.VCC, USBTTL1.5V, J1.pin1
